# Fritzing sketch WeMos_LEDstrip_Nextion_DHT (saved by Fritzing 0.9.3b)
circuit board: 5.24685cm x 8.21468cm
breadboards: 1

parts:
  LED_stripe = Neopixel Strip -- Black (30/m)
  R1 = Resistor [tolerance=±5% resistance=470 package=THT]
  IC1 = IC, DIP package, 20 pins [chip_label="SN74HCT245N " part_number=SN74HCT245N]
  Power_plug1 = Power plug
  C1 = Electrolytic Capacitor [capacitance=1µF package="100 mil [THT, electrolytic]"]
  DHT1 = DHT22 Humidity and Temperature Sensor
  WeMos_D1_Mini1 = WeMos D1 Mini
  display = female pin header, 4 pins [form="♀ (female)"]

nets:
  GND: LED_stripe.GND, IC1.pin1, IC1.pin10, IC1.pin19, Power_plug1.GND, C1.-, DHT1.GND, WeMos_D1_Mini1.G, display.pin4
  N1: LED_stripe.Din, R1.Pin_0
  +5V: LED_stripe.+5V, IC1.pin20, Power_plug1.VCC, C1.+, WeMos_D1_Mini1.5V, display.pin1
  N2: R1.Pin_1, IC1.pin3
  N3: IC1.pin17, WeMos_D1_Mini1.D3
  N4: DHT1.VDD, WeMos_D1_Mini1.D0
  N5: DHT1.DATA, WeMos_D1_Mini1.D4
  N6: WeMos_D1_Mini1.D1, display.pin2
  N7: WeMos_D1_Mini1.D2, display.pin3

custom parts:
  Neopixel Strip -- Black (30/m): These NeoPixel strips have 30 digitally-addressable pixel LEDs per meter and are very affordable and are only 12.5 mm wide, 10 mm if you remove the strip from the casing.
